# Fritzing sketch non-contact-voltage-sensor (saved by Fritzing 0.9.2b)
circuit board: 8.46667cm x 5.64444cm
breadboards: 1
perfboards: 1

parts:
  S1 = Momentary Switch [package=ksa_sealed_tac_switch]
  LED1 = smd LED [color="Red (633nm)" package="1206 [SMD]"]
  R1 = Resistor [tolerance=±5% resistance=220 package="0402 [SMD]"]
  Q1 = NPN-Transistor [package="TO92 [THT]"]
  Q2 = NPN-Transistor [package="TO92 [THT]"]
  Q3 = NPN-Transistor [package="TO92 [THT]"]
  R2 = Resistor [tolerance=±5% resistance=100k package="0402 [SMD]"]
  R3 = Resistor [tolerance=±5% resistance=1M package="0402 [SMD]"]
  VCC1 = Battery block 9V

nets:
  N1: S1.1, VCC1.+
  N2: S1.3, LED1.anode, R2.Pin_0, R3.Pin_0
  N3: LED1.cathode, R1.Pin_0
  N4: R1.Pin_1, Q1.E
  N5: Q1.B, Q2.C
  N6: Q1.C, VCC1.-
  N7: Q2.E, R2.Pin_1
  N8: Q2.B, Q3.C
  N9: Q3.E, R3.Pin_1

notes:
  Material que sirva como antena: pedaço de fio, pedaço de placa de silicio.
